// Logisim project lab_2_part3.circ as structural Verilog: 2 circuits, main circuit main
module main (
  input  Ci,
  input  a0,
  input  b0,
  input  a2,
  input  b2,
  input  a1,
  input  b1,
  input  a3,
  input  b3,
  output s0,
  output s1,
  output s2,
  output s3,
  output co
);

  wire full_adder_1_co, full_adder_2_co, full_adder_3_co;

  Full_Adder full_adder_1 (.ci(Ci), .a(a0), .b(b0), .s(s0), .co(full_adder_1_co));
  Full_Adder full_adder_2 (.ci(full_adder_1_co), .a(a1), .b(b1), .s(s1), .co(full_adder_2_co));
  Full_Adder full_adder_3 (.ci(full_adder_2_co), .a(a2), .b(b2), .s(s2), .co(full_adder_3_co));
  Full_Adder full_adder_4 (.ci(full_adder_3_co), .a(a3), .b(b3), .s(s3), .co(co));
endmodule

module Full_Adder (
  input  ci,
  input  a,
  input  b,
  output s,
  output co
);

  wire xor_1_out;

  xor xor_1 (xor_1_out, a, b);
  Multiplexer multiplexer_1 (.in0(b), .in1(ci), .out(co), .sel(xor_1_out));
  xor xor_2 (s, ci, xor_1_out);
endmodule
