// Logisim project lab3.circ as structural Verilog: 2 circuits, main circuit main
module main (
  input  D,
  output out_2,
  output out_3
);

  wire Clk_out, dff_1_qa, not_1_out;

  Clock Clk (.out(Clk_out));
  not not_1 (not_1_out, Clk_out);
  DFF dff_1 (.D(D), .Clk(not_1_out), .Qa(dff_1_qa));  // open: Qb
  DFF dff_2 (.D(dff_1_qa), .Clk(Clk_out), .Qa(out_2), .Qb(out_3));
endmodule

module DFF (
  input  D,
  input  Clk,
  output Qa,
  output Qb
);

  wire nand_1_out, nand_2_out, not_1_out;

  not not_1 (not_1_out, D);
  nand nand_1 (nand_1_out, D, Clk);
  nand nand_2 (nand_2_out, Clk, not_1_out);
  nand nand_3 (Qa, nand_1_out, Qb);
  nand nand_4 (Qb, Qa, nand_2_out);
endmodule
